# Fritzing sketch iot-raspi-mqtt-sub-01 (saved by Fritzing 0.9.9b)
breadboards: 1

parts:
  LED1 = LED - 5mm [color="Green (565nm)" current=0.030 package="5 mm [THT]"]
  LED2 = LED - 5mm [color="Yellow (595nm)" current=0.030 package="5 mm [THT]"]
  R4 = Resistor [tolerance=±5% power=0.25 resistance=560 package=THT]
  R5 = Resistor [tolerance=±5% power=0.25 resistance=560 package=THT]
  LED3 = LED - 5mm [color="Red (633nm)" current=0.030 package="5 mm [THT]"]
  R6 = Resistor [tolerance=±5% power=0.25 resistance=560 package=THT]
  Mod1 = Raspberry Pi 4B

nets:
  N1: LED1.cathode, R6.Pin_0
  N2: LED1.anode, Mod1.GPIO17
  N3: LED2.cathode, R5.Pin_0
  N4: LED2.anode, Mod1.GPIO27
  N5: R4.Pin_0, LED3.cathode
  N6: R4.Pin_1, R5.Pin_1, R6.Pin_1, Mod1.GND
  N7: LED3.anode, Mod1.GPIO22

notes:
  iot-raspi-mqtt-sub-01
